// Digital circuit LUT.dig as structural Verilog
module LUT (
  input  in_1,
  input  in_2,
  input  in_3
);

  wire dipswitch_1_out, dipswitch_2_out, dipswitch_3_out, dipswitch_4_out, dipswitch_5_out, dipswitch_6_out,
       dipswitch_7_out, dipswitch_8_out, multiplexer_1_out;

  DipSwitch dipswitch_1 (.out(dipswitch_1_out));
  DipSwitch dipswitch_2 (.out(dipswitch_2_out));
  DipSwitch dipswitch_3 (.out(dipswitch_3_out));
  DipSwitch dipswitch_4 (.out(dipswitch_4_out));
  DipSwitch dipswitch_5 (.out(dipswitch_5_out));
  DipSwitch dipswitch_6 (.out(dipswitch_6_out));
  DipSwitch dipswitch_7 (.out(dipswitch_7_out));
  DipSwitch dipswitch_8 (.out(dipswitch_8_out));
  Multiplexer #(.Selector_Bits(3)) multiplexer_1 (
    .sel({in_1, in_2, in_3}), .in_0(dipswitch_1_out), .in_1(dipswitch_2_out), .in_2(dipswitch_3_out),
    .in_3(dipswitch_4_out), .in_4(dipswitch_5_out), .in_5(dipswitch_6_out), .in_6(dipswitch_7_out),
    .in_7(dipswitch_8_out), .out(multiplexer_1_out));
  LED led_1 (.in(multiplexer_1_out));
endmodule
