// Digital circuit latchFlipFlop.dig as structural Verilog
module latchFlipFlop (
  input  D,
  input  En,
  output Q,
  output Q2
);

  wire and_1_out, and_2_out, not_1_out;

  not not_1 (not_1_out, D);
  and and_1 (and_1_out, D, En);
  and and_2 (and_2_out, En, not_1_out);
  D_FF d_ff_1 (.D(D), .C(En), .Q(Q2));  // open: nQ
  RS_FF_AS rs_ff_as_1 (.S(and_1_out), .R(and_2_out), .Q(Q));  // open: nQ
endmodule
