// Digital circuit latchTransparente.dig as structural Verilog
module latchTransparente (
  input  EN,
  input  D,
  output Q
);

  wire not_1_out, not_2_out, transgate_1_out2;

  not not_1 (not_1_out, EN);
  TransGate transgate_1 (.A(EN), .nA(not_1_out), .out1(D), .out2(transgate_1_out2));
  not not_2 (not_2_out, transgate_1_out2);
  TransGate transgate_2 (.A(not_1_out), .nA(EN), .out1(Q), .out2(transgate_1_out2));
  not not_3 (Q, not_2_out);
endmodule
