// Digital circuit shiftReg.dig as structural Verilog
module shiftReg (
  input  ck,
  input  load_shift,
  input  d_3,
  input  d_2,
  input  d_1,
  input  d_0,
  input  s_in,
  output q_0,
  output s_out,
  output q_1,
  output q_2,
  output q_3
);

  wire multiplexer_1_out, multiplexer_2_out, multiplexer_3_out, multiplexer_4_out;

  Multiplexer multiplexer_1 (.sel(load_shift), .in_0(d_3), .in_1(q_2), .out(multiplexer_1_out));
  Multiplexer multiplexer_2 (.sel(load_shift), .in_0(d_2), .in_1(q_1), .out(multiplexer_2_out));
  Multiplexer multiplexer_3 (.sel(load_shift), .in_0(d_1), .in_1(q_0), .out(multiplexer_3_out));
  Multiplexer multiplexer_4 (.sel(load_shift), .in_0(d_0), .in_1(s_in), .out(multiplexer_4_out));
  D_FF d_ff_1 (.D(multiplexer_1_out), .C(ck), .Q(q_3));  // open: nQ
  D_FF d_ff_2 (.D(multiplexer_2_out), .C(ck), .Q(q_2));  // open: nQ
  D_FF d_ff_3 (.D(multiplexer_3_out), .C(ck), .Q(q_1));  // open: nQ
  D_FF d_ff_4 (.D(multiplexer_4_out), .C(ck), .Q(q_0));  // open: nQ

  assign s_out = q_3;
endmodule
